# Fritzing sketch cosilino-device-plan (saved by Fritzing 0.9.3b)
circuit board: 8.46667cm x 5.64444cm

parts:
  U1 = NodeMCU V3.0
  R1 = Resistor [tolerance=±5% resistance=220 package=THT]
  LED1 = LED - 5mm [color="Red (633nm)" package="5 mm [THT]"]
  R2 = Resistor [tolerance=±5% resistance=220 package=THT]
  LED2 = LED - 5mm [color="Orange (612nm)" package="5 mm [THT]"]
  R3 = Resistor [tolerance=±5% resistance=220 package=THT]
  LED3 = LED - 5mm [color="Green (565nm)" package="5 mm [THT]"]
  J1 = Basic Servo
  DHT22 = Humidity and Temperature Sensor RHT03
  DS18S20 = TEMPERATURE-SENSOR [package=to-92]

nets:
  N1: U1.D1, J1.pulse
  N2: U1.D2, DS18S20.ADJ
  N3: U1.D3, DHT22.Data-signal
  VCC: U1.3V3, DHT22.Vcc, DS18S20.VCC
  GND: U1.GND, LED1.cathode, LED2.cathode, LED3.cathode, J1.gnd, DHT22.GND_2, DS18S20.GND
  N4: U1.D6, R3.Pin_1
  N5: U1.D7, R2.Pin_1
  N6: U1.D8, R1.Pin_1
  N7: U1.VU, J1.vcc
  N8: R1.Pin_0, LED1.anode
  N9: R2.Pin_0, LED2.anode
  N10: R3.Pin_0, LED3.anode

custom parts:
  NodeMCU V3.0: ESP8266 based NodeMCU
